// Logisim project GangeMedTi.circ as structural Verilog: 4 circuits, main circuit Half Adder
module Half_Adder (
  input  X_inn,
  input  Y_inn,
  output Sum,
  output Cout
);

  and and_1 (Cout, X_inn, Y_inn);
  xor xor_1 (Sum, X_inn, Y_inn);
endmodule

module Full_Adder (
  input  X_inn,
  input  Y_inn,
  input  C_inn,
  output Sum,
  output Cout
);

  wire and_1_out, and_2_out, and_3_out, xor_1_out;

  xor xor_1 (xor_1_out, X_inn, Y_inn);
  and and_1 (and_1_out, X_inn, Y_inn);
  and and_2 (and_2_out, X_inn, C_inn);
  and and_3 (and_3_out, C_inn, Y_inn);
  xor xor_2 (Sum, xor_1_out, C_inn);
  or or_1 (Cout, and_1_out, and_2_out, and_3_out);
endmodule

module mul10 (
  input  in_1,
  input  in_2,
  input  in_3,
  input  in_4,
  input  in_5,
  output out_6,
  output out_7,
  output out_8,
  output out_9,
  output out_10,
  output out_11,
  output out_12,
  output out_13,
  output out_14
);

  wire full_adder_1_sum, full_adder_2_sum, full_adder_3_sum, full_adder_4_sum, full_adder_5_sum,
       full_adder_6_sum, full_adder_7_sum, full_adder_8_sum, full_adder_9_sum, full_adder_10_sum,
       full_adder_11_sum, full_adder_12_sum, full_adder_13_sum, full_adder_14_sum, full_adder_15_sum,
       full_adder_16_sum, half_adder_2_sum, half_adder_3_sum, half_adder_4_sum, half_adder_5_sum,
       half_adder_6_sum, half_adder_7_sum, half_adder_8_sum, half_adder_9_sum, half_adder_10_sum,
       half_adder_11_sum, half_adder_12_sum, half_adder_13_sum, half_adder_14_sum, undriven, undriven_2,
       undriven_3, undriven_4, undriven_5, undriven_6, undriven_7, undriven_8, undriven_9, undriven_10,
       undriven_11, undriven_12, undriven_13, undriven_14, undriven_15, undriven_16, undriven_17,
       undriven_18, undriven_19, undriven_20, undriven_21, undriven_22, xor_1_out, xor_2_out, xor_3_out,
       xor_4_out, xor_5_out, xor_6_out, xor_7_out, xor_8_out;

  xor xor_1 (xor_1_out, in_1, half_adder_3_sum);
  Half_Adder half_adder_1 (.X_inn(xor_1_out), .Y_inn(half_adder_2_sum));  // open: Sum, Cout
  xor xor_2 (xor_2_out, in_1, undriven);
  Half_Adder half_adder_2 (.Sum(half_adder_2_sum), .X_inn(xor_2_out), .Y_inn(half_adder_4_sum));  // open: Cout
  Half_Adder half_adder_3 (.Sum(half_adder_3_sum), .X_inn(full_adder_1_sum), .Y_inn(half_adder_5_sum));  // open: Cout
  xor xor_3 (xor_3_out, in_1, undriven_2);
  Half_Adder half_adder_4 (.Sum(half_adder_4_sum), .X_inn(xor_3_out), .Y_inn(half_adder_6_sum));  // open: Cout
  Full_Adder full_adder_1 (
    .Sum(full_adder_1_sum), .X_inn(full_adder_2_sum), .Y_inn(full_adder_2_sum), .C_inn(full_adder_3_sum));  // open: Cout
  Half_Adder half_adder_5 (.Sum(half_adder_5_sum), .X_inn(undriven_3), .Y_inn(full_adder_4_sum));  // open: Cout
  xor xor_4 (xor_4_out, in_1, undriven_4);
  Half_Adder half_adder_6 (.Sum(half_adder_6_sum), .X_inn(xor_4_out), .Y_inn(half_adder_7_sum));  // open: Cout
  Full_Adder full_adder_2 (
    .Sum(full_adder_2_sum), .X_inn(full_adder_8_sum), .Y_inn(full_adder_8_sum), .C_inn(full_adder_5_sum));  // open: Cout
  Full_Adder full_adder_3 (
    .Sum(full_adder_3_sum), .X_inn(undriven_6), .Y_inn(undriven_6), .C_inn(full_adder_6_sum));  // open: Cout
  Full_Adder full_adder_4 (
    .Sum(full_adder_4_sum), .X_inn(undriven_5), .Y_inn(full_adder_8_sum), .C_inn(full_adder_7_sum));  // open: Cout
  xor xor_5 (xor_5_out, in_1, undriven_7);
  Half_Adder half_adder_7 (.Sum(half_adder_7_sum), .X_inn(xor_5_out), .Y_inn(half_adder_8_sum));  // open: Cout
  Full_Adder full_adder_5 (
    .Sum(full_adder_5_sum), .X_inn(undriven_11), .Y_inn(undriven_11), .C_inn(full_adder_9_sum));  // open: Cout
  Full_Adder full_adder_6 (
    .Sum(full_adder_6_sum), .X_inn(undriven_9), .Y_inn(undriven_9), .C_inn(full_adder_10_sum));  // open: Cout
  Full_Adder full_adder_7 (
    .Sum(full_adder_7_sum), .X_inn(undriven_8), .Y_inn(undriven_11), .C_inn(full_adder_11_sum));  // open: Cout
  xor xor_6 (xor_6_out, in_1, undriven_10);
  Half_Adder half_adder_8 (.Sum(half_adder_8_sum), .X_inn(xor_6_out), .Y_inn(half_adder_9_sum));  // open: Cout
  Full_Adder full_adder_8 (
    .Sum(full_adder_8_sum), .X_inn(in_2), .Y_inn(in_2), .C_inn(full_adder_12_sum));  // open: Cout
  Full_Adder full_adder_9 (
    .Sum(full_adder_9_sum), .X_inn(undriven_15), .Y_inn(undriven_15), .C_inn(full_adder_13_sum));  // open: Cout
  Full_Adder full_adder_10 (
    .Sum(full_adder_10_sum), .X_inn(undriven_13), .Y_inn(undriven_13), .C_inn(full_adder_14_sum));  // open: Cout
  Full_Adder full_adder_11 (
    .Sum(full_adder_11_sum), .X_inn(undriven_12), .Y_inn(undriven_15), .C_inn(full_adder_15_sum));  // open: Cout
  xor xor_7 (xor_7_out, in_1, undriven_14);
  Half_Adder half_adder_9 (.Sum(half_adder_9_sum), .X_inn(xor_7_out), .Y_inn(half_adder_10_sum));  // open: Cout
  Full_Adder full_adder_12 (
    .Sum(full_adder_12_sum), .X_inn(in_3), .Y_inn(in_3), .C_inn(full_adder_16_sum));  // open: Cout
  Full_Adder full_adder_13 (
    .Sum(full_adder_13_sum), .X_inn(undriven_19), .Y_inn(undriven_19), .C_inn(half_adder_11_sum));  // open: Cout
  Full_Adder full_adder_14 (
    .Sum(full_adder_14_sum), .X_inn(undriven_17), .Y_inn(undriven_17), .C_inn(half_adder_12_sum));  // open: Cout
  Full_Adder full_adder_15 (
    .Sum(full_adder_15_sum), .X_inn(undriven_16), .Y_inn(undriven_19), .C_inn(half_adder_13_sum));  // open: Cout
  xor xor_8 (xor_8_out, in_1, undriven_18);
  Half_Adder half_adder_10 (.Sum(half_adder_10_sum), .X_inn(xor_8_out), .Y_inn(in_1));  // open: Cout
  Full_Adder full_adder_16 (
    .Sum(full_adder_16_sum), .X_inn(in_4), .Y_inn(in_4), .C_inn(half_adder_14_sum));  // open: Cout
  Half_Adder half_adder_11 (.Sum(half_adder_11_sum), .X_inn(undriven_22), .Y_inn(undriven_22));  // open: Cout
  Half_Adder half_adder_12 (.Sum(half_adder_12_sum), .X_inn(undriven_21), .Y_inn(undriven_21));  // open: Cout
  Half_Adder half_adder_13 (.Sum(half_adder_13_sum), .X_inn(undriven_20), .Y_inn(undriven_22));  // open: Cout
  Half_Adder half_adder_14 (.Sum(half_adder_14_sum), .X_inn(in_5), .Y_inn(in_5));  // open: Cout

  assign out_6 = in_1;
endmodule

module mul10_v2 (
  input  [3:0] in_1,
  output [8:0] out_2
);

  wire full_adder_1_cout, half_adder_1_cout, half_adder_2_cout;

  Half_Adder half_adder_1 (.Sum(out_2[3]), .Cout(half_adder_1_cout), .X_inn(in_1[2]), .Y_inn(in_1[0]));
  Full_Adder full_adder_1 (
    .Sum(out_2[4]), .Cout(full_adder_1_cout), .X_inn(in_1[3]), .Y_inn(in_1[1]), .C_inn(half_adder_1_cout));
  Half_Adder half_adder_2 (.Sum(out_2[5]), .Cout(half_adder_2_cout), .X_inn(in_1[2]), .Y_inn(full_adder_1_cout));
  Half_Adder half_adder_3 (.Sum(out_2[6]), .Cout(out_2[7]), .X_inn(in_1[3]), .Y_inn(half_adder_2_cout));

  assign out_2[2:0] = {in_1[1:0], 1'b0};
endmodule
