// Logisim project Oblig2.circ as structural Verilog: 4 circuits, main circuit main
module main (
);

  wire clock_1_out, decoder_1_out_2, decoder_1_out_3, decoder_1_out_4, decoder_1_out_5, not_1_out, or_1_out,
       or_2_out, or_3_out, R_out;
  wire [3:0] counter_1_out;
  wire [7:0] controlled_buffer_1_out, overwrite_lsb_msb_1_output, R_2_q, ram_1_data, ram_2_data;

  Clock clock_1 (.out(clock_1_out));
  Counter counter_1 (.Clock(clock_1_out), .Reset(R_out), .Out(counter_1_out));
  Button R (.out(R_out));
  RAM #(.addrWidth(4), .bus("asynch")) ram_1 (
    .addr(counter_1_out), .data(ram_1_data), .sel(1'b1), .ld(1'b1), .clr(1'b0));
  Decoder decoder_1 (
    .in_1(ram_1_data[7:4]), .out_2(decoder_1_out_2), .out_4(decoder_1_out_4), .out_5(decoder_1_out_5),
    .out_3(decoder_1_out_3));
  assign controlled_buffer_1_out = or_1_out ? overwrite_lsb_msb_1_output : 8'bz;  // Controlled_Buffer controlled_buffer_1
  Overwrite_LSB_MSB overwrite_lsb_msb_1 (
    .Initial_value(R_2_q), .bits_to_overwrite_LSB_MSB(ram_1_data[3:0]),
    .Overwrite__LSB_when_0__MSB_when_1(not_1_out), .Output(overwrite_lsb_msb_1_output));
  not not_1 (not_1_out, decoder_1_out_2);
  or or_1 (or_1_out, decoder_1_out_2, decoder_1_out_4);
  or or_2 (or_2_out, decoder_1_out_5, decoder_1_out_3);
  or or_3 (or_3_out, or_1_out, decoder_1_out_5);
  assign controlled_buffer_1_out = decoder_1_out_5 ? ram_2_data : 8'bz;  // Controlled_Buffer controlled_buffer_2
  RAM #(.addrWidth(4)) ram_2 (
    .addr(ram_1_data[3:0]), .data(ram_2_data), .sel(or_2_out), .clk(clock_1_out), .ld(decoder_1_out_5),
    .clr(R_out));
  Register #(.trigger("falling")) R_2 (
    .D(controlled_buffer_1_out), .en(or_3_out), .Q(R_2_q), .clk(clock_1_out), .clr(R_out));
  assign ram_2_data = decoder_1_out_3 ? R_2_q : 8'bz;  // Controlled_Buffer controlled_buffer_3
endmodule

// Count
module Counter (
  input  Clock,
  input  Reset,
  output [3:0] Out
);

  wire adder_1_cout, not_1_out;
  wire [3:0] adder_1_out;

  not not_1 (not_1_out, adder_1_cout);
  Register #(.width(4), .trigger("falling")) register_1 (
    .D(adder_1_out), .en(not_1_out), .Q(Out), .clk(Clock), .clr(Reset));
  Adder #(.width(4)) adder_1 (.a(Out), .b(4'b0001), .out(adder_1_out), .cout(adder_1_cout));  // open: cin
endmodule

// OW
module Overwrite_LSB_MSB (
  input  [7:0] Initial_value,
  input  [3:0] bits_to_overwrite_LSB_MSB,
  input  Overwrite__LSB_when_0__MSB_when_1,
  output [7:0] Output
);

  wire not_1_out, not_2_out;

  not not_1 (not_1_out, Overwrite__LSB_when_0__MSB_when_1);
  assign Output[3:0] = Overwrite__LSB_when_0__MSB_when_1 ? Initial_value[3:0] : 4'bz;  // Controlled_Buffer controlled_buffer_1
  assign Output[7:4] = not_1_out ? Initial_value[7:4] : 4'bz;  // Controlled_Buffer controlled_buffer_2
  assign Output[3:0] = not_2_out ? bits_to_overwrite_LSB_MSB : 4'bz;  // Controlled_Buffer controlled_buffer_3
  assign Output[7:4] = Overwrite__LSB_when_0__MSB_when_1 ? bits_to_overwrite_LSB_MSB : 4'bz;  // Controlled_Buffer controlled_buffer_4
  not not_2 (not_2_out, Overwrite__LSB_when_0__MSB_when_1);
endmodule

module Decoder (
  input  [3:0] in_1,
  output out_2,
  output out_3,
  output out_4,
  output out_5
);

  Decoder_part #(.select(4), .enable("false")) decoder_1 (
    .out8(out_2), .out9(out_4), .out10(out_5), .out11(out_3), .sel(in_1));  // open: out0, out1, out2, out3, out4, out5, out6, out7, out12, out13, out14, out15
endmodule
