// Logisim project Oppgave1.circ as structural Verilog
module Counter (
  input  in_1,
  input  [3:0] in_2
);

  wire adder_1_cout, clock_1_out;
  wire [3:0] adder_1_out, register_1_q;

  Clock clock_1 (.out(clock_1_out));
  Register #(.width(4)) register_1 (.D(adder_1_out), .en(in_1), .Q(register_1_q), .clk(clock_1_out), .clr(1'b0));
  Adder #(.width(4)) adder_1 (.a(register_1_q), .b(in_2), .out(adder_1_out), .cin(1'b0), .cout(adder_1_cout));
  // also tied to GND on the sheet: adder_1_cout
endmodule
